# Fritzing sketch receiver (saved by Fritzing 0.9.10b)
circuit board: 6.12331cm x 4.33454cm

parts:
  U1 = ESP32-38PinWide [part_number=ESP32]
  Whadda_433_TX = mystery part, 3 pins [chip_label=?]

nets:
  N1: U1.P34, Whadda_433_TX.pin1
  GND: U1.GND, Whadda_433_TX.pin3
  N2: U1.VIN, Whadda_433_TX.pin2

notes:
  alicescfernandes
  SIG VCC GND

custom parts:
  ESP32-38PinWide: Generic 38-Pin ESP32 with wide format (only access to one side of pins on a breadboard) based on Stephen Lilley's HiLetgo ESP-WROOM-32 ESP32 ESP-32S Development Board.
